// Logisim project ai.circ as structural Verilog: 1 circuit, main circuit main
module main (
  input  [7:0] in_1
);

  // Probe on nothing
  // CdM_8_mark5 cdm_8_mark5_1: pin names not known; wires that end beside it: in_1
  RAM ram_1 ();  // open: addr, data, sel, clk, ld, clr
endmodule
